// Logisim project WISHAH NASEER DATAPATH.circ as structural Verilog: 9 circuits, main circuit main
module main (
  input  in_1,
  input  in_2,
  output out_3
);

  wire alu_controller_1_branch_2, and_1_out, clock_1_out, control_unit_1_out_2, control_unit_1_out_3,
       control_unit_1_out_4, control_unit_1_out_5, control_unit_1_out_6, control_unit_1_out_8,
       control_unit_1_out_9, control_unit_1_out_10;
  wire [2:0] control_unit_1_out_7;
  wire [31:0] adder_1_out, alu_controller_1_output, immidiate_generation_1_out_3,
       immidiate_generation_1_out_4, immidiate_generation_1_out_5, multiplexer_1_out, multiplexer_2_out,
       multiplexer_3_out, multiplexer_4_out, multiplexer_5_out, n32_bit_register_file_1_readdata1,
       n32_bit_register_file_1_readdata2, ram_1_data, register_1_q, rom_1_data;

  Clock clock_1 (.out(clock_1_out));
  Register #(.width(32)) register_1 (
    .D(multiplexer_1_out), .Q(register_1_q), .clk(clock_1_out), .clr(in_1));  // open: en
  Multiplexer #(.width(32), .enable("false")) multiplexer_1 (
    .in0(adder_1_out), .in1(multiplexer_2_out), .out(multiplexer_1_out), .sel(control_unit_1_out_10));
  Adder #(.width(32)) adder_1 (.a(register_1_q), .b(32'h4), .out(adder_1_out));  // open: cin, cout
  Multiplexer #(.width(32), .enable("false")) multiplexer_2 (
    .in0(adder_1_out), .in1(immidiate_generation_1_out_4), .out(multiplexer_2_out), .sel(and_1_out));
  ROM #(.addrWidth(20), .dataWidth(32)) rom_1 (.addr(register_1_q[21:2]), .data(rom_1_data));  // open: sel
  // Probe on rom_1_data
  // Probe on rom_1_data[6:0]
  // Probe on rom_1_data[14:12]
  // Probe on rom_1_data[30]
  // Probe on rom_1_data[25]
  CONTROL_UNIT control_unit_1 (
    .in_1(rom_1_data[6:0]), .out_2(control_unit_1_out_2), .out_3(control_unit_1_out_3),
    .out_4(control_unit_1_out_4), .out_5(control_unit_1_out_5), .out_6(control_unit_1_out_6),
    .out_7(control_unit_1_out_7), .out_8(control_unit_1_out_8), .out_9(control_unit_1_out_9),
    .out_10(control_unit_1_out_10));
  // Probe on rom_1_data[24:20]
  // Probe on rom_1_data[19:15]
  // Probe on rom_1_data[24:20]
  and and_1 (and_1_out, alu_controller_1_branch_2, control_unit_1_out_3);
  // Probe on n32_bit_register_file_1_readdata2
  // Probe on n32_bit_register_file_1_readdata1
  _32_BIT_REGISTER_FILE u_32_bit_register_file_1 (
    .ReadReg1(rom_1_data[19:15]), .ReadReg2(rom_1_data[24:20]), .WriteReg(rom_1_data[11:7]),
    .RegWrite(control_unit_1_out_5), .WriteData(multiplexer_5_out), .Clk(clock_1_out),
    .ReadData1(n32_bit_register_file_1_readdata1), .ReadData2(n32_bit_register_file_1_readdata2), .Reset(in_2));
  IMMIDIATE_GENERATION immidiate_generation_1 (
    .out_3(immidiate_generation_1_out_3), .in_1(rom_1_data), .out_4(immidiate_generation_1_out_4),
    .in_2(register_1_q), .out_5(immidiate_generation_1_out_5));
  Multiplexer #(.width(32), .enable("false")) multiplexer_3 (
    .in0(n32_bit_register_file_1_readdata2), .in1(multiplexer_4_out), .out(multiplexer_3_out),
    .sel(control_unit_1_out_8));
  Multiplexer #(.width(32), .enable("false")) multiplexer_4 (
    .in0(immidiate_generation_1_out_5), .in1(immidiate_generation_1_out_3), .out(multiplexer_4_out),
    .sel(control_unit_1_out_9));
  // Probe on control_unit_1_out_7
  ALU_CONTROLLER alu_controller_1 (
    .OPCODE(rom_1_data[6:0]), .OPERAND_A(n32_bit_register_file_1_readdata1), .F7(rom_1_data[30]),
    .OPERAND_B(multiplexer_3_out), .F3(rom_1_data[14:12]), .ALU_OP(control_unit_1_out_7), .out_9(out_3),
    .\output (alu_controller_1_output), .branch(control_unit_1_out_3), .BRANCH_2(alu_controller_1_branch_2),
    ._25th_bit(rom_1_data[25]));
  // Probe on alu_controller_1_output
  // Probe on multiplexer_3_out
  RAM #(.dataWidth(32), .bus("separate")) ram_1 (
    .addr(alu_controller_1_output[9:2]), .din(n32_bit_register_file_1_readdata2), .data(ram_1_data),
    .str(control_unit_1_out_2), .clk(clock_1_out), .ld(control_unit_1_out_4));  // open: sel, clr
  Multiplexer #(.width(32), .enable("false")) multiplexer_5 (
    .in0(alu_controller_1_output), .in1(ram_1_data), .out(multiplexer_5_out), .sel(control_unit_1_out_6));
  // Probe on ram_1_data
  // Probe on multiplexer_5_out

  // Notes on the sheet:
  //   WISHAH NASEER
  //   18B-016-CE
endmodule

module PROGRAM_COUNTER (
  input  in_1,
  output [31:0] out_2
);

  wire [31:0] adder_1_out;

  Register #(.width(32)) register_1 (.D(adder_1_out), .Q(out_2), .clk(in_1));  // open: en, clr
  Adder #(.width(32)) adder_1 (.a(32'h4), .b(out_2), .out(adder_1_out));  // open: cin, cout
  RAM #(.addrWidth(10), .dataWidth(32)) ram_1 (.addr(out_2[11:2]));  // open: data, sel, clk, ld, clr
endmodule

module TYPE_DECODE (
  input  [6:0] in_1,
  output R_TYPE,
  output LOAD,
  output STORE,
  output I_TYPE,
  output branch
);

  Comparator #(.width(7)) comparator_1 (.a(in_1), .b(7'b0110011), .eq(R_TYPE));  // open: gt, lt
  Comparator #(.width(7)) comparator_2 (.a(in_1), .b(7'b0000011), .eq(LOAD));  // open: gt, lt
  Comparator #(.width(7)) comparator_3 (.a(in_1), .b(7'b0100011), .eq(STORE));  // open: gt, lt
  Comparator #(.width(7)) comparator_4 (.a(in_1), .b(7'b0010011), .eq(I_TYPE));  // open: gt, lt
  Comparator #(.width(7)) comparator_5 (.a(in_1), .b(7'b1100011), .eq(branch));  // open: gt, lt
endmodule

module CONTROL_DECODE (
  input  R_type,
  input  Load,
  input  store,
  input  I_type,
  input  branch,
  output memwrite,
  output branch_2,
  output memread,
  output regwrite,
  output memtoreg,
  output [2:0] ALU_OP,
  output OPERAND_B_SEL,
  output EXTEND_SELECT,
  output next_pc_select
);

  or or_1 (regwrite, R_type, Load, I_type);
  or or_2 (OPERAND_B_SEL, Load, store, I_type);
  ALU_OP alu_op_1 (.R_Type(R_type), .Load(Load), .Store(store), .I_Type(I_type), .Branch(branch), .out_6(ALU_OP));

  assign branch_2 = branch;
  assign EXTEND_SELECT = store;
  assign memread = Load;
  assign memtoreg = Load;
  assign memwrite = store;
  assign next_pc_select = branch;
endmodule

module ALU_OP (
  input  R_Type,
  input  Load,
  input  Store,
  input  I_Type,
  input  Branch,
  output [2:0] out_6
);

  wire not_1_out, not_2_out, not_3_out, not_4_out, not_5_out, not_6_out, not_7_out, not_8_out, not_9_out,
       not_10_out;

  not not_1 (not_1_out, R_Type);
  not not_2 (not_2_out, Branch);
  not not_3 (not_3_out, I_Type);
  not not_4 (not_4_out, R_Type);
  not not_5 (not_5_out, Load);
  not not_6 (not_6_out, Store);
  not not_7 (not_7_out, I_Type);
  not not_8 (not_8_out, R_Type);
  not not_9 (not_9_out, Load);
  not not_10 (not_10_out, Branch);
  and and_1 (out_6[1], not_4_out, not_5_out, not_6_out, not_7_out);
  and and_2 (out_6[2], not_1_out, not_2_out, not_3_out);
  and and_3 (out_6[0], not_8_out, not_10_out, not_9_out);
endmodule

// REGISTER FILE
module _32_BIT_REGISTER_FILE (
  input  [4:0] ReadReg1,
  input  [4:0] ReadReg2,
  input  [4:0] WriteReg,
  input  RegWrite,
  input  [31:0] WriteData,
  input  Clk,
  input  Reset,
  output [31:0] ReadData1,
  output [31:0] ReadData2
);

  wire decoder_1_out0, decoder_1_out1, decoder_2_out0, decoder_2_out1, decoder_2_out2, decoder_2_out3,
       decoder_3_out0, decoder_3_out1, decoder_3_out2, decoder_3_out3, decoder_4_out0, decoder_4_out1,
       decoder_4_out2, decoder_4_out3, decoder_5_out0, decoder_5_out1, decoder_5_out2, decoder_5_out3,
       decoder_6_out0, decoder_6_out1, decoder_6_out2, decoder_6_out3, decoder_7_out0, decoder_7_out1,
       decoder_7_out2, decoder_7_out3, decoder_8_out0, decoder_8_out1, decoder_8_out2, decoder_8_out3,
       decoder_9_out0, decoder_9_out1, decoder_9_out2, decoder_9_out3, decoder_10_out0, decoder_10_out1,
       decoder_10_out2, decoder_10_out3, decoder_11_out0, decoder_11_out1, decoder_11_out2, decoder_11_out3;
  wire [31:0] multiplexer_1_out, multiplexer_2_out, multiplexer_3_out, multiplexer_4_out, multiplexer_5_out,
       multiplexer_6_out, multiplexer_7_out, multiplexer_8_out, multiplexer_9_out, multiplexer_10_out,
       multiplexer_13_out, multiplexer_14_out, multiplexer_15_out, multiplexer_16_out, multiplexer_17_out,
       multiplexer_18_out, multiplexer_19_out, multiplexer_20_out, multiplexer_21_out, multiplexer_22_out,
       register_1_q, register_2_q, register_3_q, register_4_q, register_5_q, register_6_q, register_7_q,
       register_8_q, register_9_q, register_10_q, register_11_q, register_12_q, register_13_q, register_14_q,
       register_15_q, register_16_q, register_17_q, register_18_q, register_19_q, register_20_q,
       register_21_q, register_22_q, register_23_q, register_24_q, register_25_q, register_26_q,
       register_27_q, register_28_q, register_29_q, register_30_q, register_31_q;

  // Probe on WriteReg
  Decoder #(.disabled(0)) decoder_1 (.out0(decoder_1_out0), .out1(decoder_1_out1), .sel(WriteReg[4]), .en(RegWrite));
  Decoder #(.select(2), .disabled(0)) decoder_2 (
    .out0(decoder_2_out0), .out1(decoder_2_out1), .out2(decoder_2_out2), .out3(decoder_2_out3),
    .sel(WriteReg[3:2]), .en(decoder_1_out0));
  Decoder #(.select(2), .disabled(0)) decoder_3 (
    .out0(decoder_3_out0), .out1(decoder_3_out1), .out2(decoder_3_out2), .out3(decoder_3_out3),
    .sel(WriteReg[1:0]), .en(decoder_2_out0));
  Decoder #(.select(2), .disabled(0)) decoder_4 (
    .out0(decoder_4_out0), .out1(decoder_4_out1), .out2(decoder_4_out2), .out3(decoder_4_out3),
    .sel(WriteReg[1:0]), .en(decoder_2_out1));
  Decoder #(.select(2), .disabled(0)) decoder_5 (
    .out0(decoder_5_out0), .out1(decoder_5_out1), .out2(decoder_5_out2), .out3(decoder_5_out3),
    .sel(WriteReg[1:0]), .en(decoder_2_out2));
  Decoder #(.select(2), .disabled(0)) decoder_6 (
    .out0(decoder_6_out0), .out1(decoder_6_out1), .out2(decoder_6_out2), .out3(decoder_6_out3),
    .sel(WriteReg[1:0]), .en(decoder_2_out3));
  Register #(.width(32)) register_1 (.D(WriteData), .en(decoder_3_out1), .Q(register_1_q), .clk(Clk), .clr(Reset));
  Register #(.width(32)) register_2 (.D(WriteData), .en(decoder_3_out2), .Q(register_2_q), .clk(Clk), .clr(Reset));
  Register #(.width(32)) register_3 (.D(WriteData), .en(decoder_3_out3), .Q(register_3_q), .clk(Clk), .clr(Reset));
  Register #(.width(32)) register_4 (.D(WriteData), .en(decoder_4_out0), .Q(register_4_q), .clk(Clk), .clr(Reset));
  Register #(.width(32)) register_5 (.D(WriteData), .en(decoder_4_out1), .Q(register_5_q), .clk(Clk), .clr(Reset));
  Register #(.width(32)) register_6 (.D(WriteData), .en(decoder_4_out2), .Q(register_6_q), .clk(Clk), .clr(Reset));
  Register #(.width(32)) register_7 (.D(WriteData), .en(decoder_4_out3), .Q(register_7_q), .clk(Clk), .clr(Reset));
  Register #(.width(32)) register_8 (.D(WriteData), .en(decoder_5_out0), .Q(register_8_q), .clk(Clk), .clr(Reset));
  Register #(.width(32)) register_9 (.D(WriteData), .en(decoder_5_out1), .Q(register_9_q), .clk(Clk), .clr(Reset));
  Register #(.width(32)) register_10 (.D(WriteData), .en(decoder_5_out2), .Q(register_10_q), .clk(Clk), .clr(Reset));
  Register #(.width(32)) register_11 (.D(WriteData), .en(decoder_5_out3), .Q(register_11_q), .clk(Clk), .clr(Reset));
  Register #(.width(32)) register_12 (.D(WriteData), .en(decoder_6_out0), .Q(register_12_q), .clk(Clk), .clr(Reset));
  Register #(.width(32)) register_13 (.D(WriteData), .en(decoder_6_out1), .Q(register_13_q), .clk(Clk), .clr(Reset));
  Register #(.width(32)) register_14 (.D(WriteData), .en(decoder_6_out2), .Q(register_14_q), .clk(Clk), .clr(Reset));
  Register #(.width(32)) register_15 (.D(WriteData), .en(decoder_6_out3), .Q(register_15_q), .clk(Clk), .clr(Reset));
  // Probe on {32{1'b0}}
  // Probe on register_1_q
  // Probe on register_2_q
  // Probe on register_3_q
  // Probe on register_4_q
  // Probe on register_5_q
  // Probe on register_6_q
  // Probe on register_7_q
  // Probe on register_8_q
  // Probe on register_9_q
  // Probe on register_10_q
  // Probe on register_11_q
  // Probe on register_12_q
  // Probe on register_13_q
  // Probe on register_14_q
  // Probe on register_15_q
  // Probe on ReadReg1
  Multiplexer #(.select(2), .width(32), .enable("false")) multiplexer_1 (
    .in0({32{1'b0}}), .in1(register_1_q), .in2(register_2_q), .in3(register_3_q), .out(multiplexer_1_out),
    .sel(ReadReg1[1:0]));
  Multiplexer #(.select(2), .width(32), .enable("false")) multiplexer_2 (
    .in0(register_4_q), .in1(register_5_q), .in2(register_6_q), .in3(register_7_q), .out(multiplexer_2_out),
    .sel(ReadReg1[1:0]));
  Multiplexer #(.select(2), .width(32), .enable("false")) multiplexer_3 (
    .in0(register_8_q), .in1(register_9_q), .in2(register_10_q), .in3(register_11_q),
    .out(multiplexer_3_out), .sel(ReadReg1[1:0]));
  Multiplexer #(.select(2), .width(32), .enable("false")) multiplexer_4 (
    .in0(register_12_q), .in1(register_13_q), .in2(register_14_q), .in3(register_15_q),
    .out(multiplexer_4_out), .sel(ReadReg1[1:0]));
  // Probe on ReadReg2
  Multiplexer #(.select(2), .width(32), .enable("false")) multiplexer_5 (
    .in0({32{1'b0}}), .in1(register_1_q), .in2(register_2_q), .in3(register_3_q), .out(multiplexer_5_out),
    .sel(ReadReg2[1:0]));
  Multiplexer #(.select(2), .width(32), .enable("false")) multiplexer_6 (
    .in0(register_4_q), .in1(register_5_q), .in2(register_6_q), .in3(register_7_q), .out(multiplexer_6_out),
    .sel(ReadReg2[1:0]));
  Multiplexer #(.select(2), .width(32), .enable("false")) multiplexer_7 (
    .in0(register_8_q), .in1(register_9_q), .in2(register_10_q), .in3(register_11_q),
    .out(multiplexer_7_out), .sel(ReadReg2[1:0]));
  Multiplexer #(.select(2), .width(32), .enable("false")) multiplexer_8 (
    .in0(register_12_q), .in1(register_13_q), .in2(register_14_q), .in3(register_15_q),
    .out(multiplexer_8_out), .sel(ReadReg2[1:0]));
  Multiplexer #(.select(2), .width(32), .enable("false")) multiplexer_9 (
    .in0(multiplexer_5_out), .in1(multiplexer_6_out), .in2(multiplexer_7_out), .in3(multiplexer_8_out),
    .out(multiplexer_9_out), .sel(ReadReg2[3:2]));
  Multiplexer #(.select(2), .width(32), .enable("false")) multiplexer_10 (
    .in0(multiplexer_1_out), .in1(multiplexer_2_out), .in2(multiplexer_3_out), .in3(multiplexer_4_out),
    .out(multiplexer_10_out), .sel(ReadReg1[3:2]));
  Decoder #(.select(2), .disabled(0)) decoder_7 (
    .out0(decoder_7_out0), .out1(decoder_7_out1), .out2(decoder_7_out2), .out3(decoder_7_out3),
    .sel(WriteReg[3:2]), .en(decoder_1_out1));
  Decoder #(.select(2), .disabled(0)) decoder_8 (
    .out0(decoder_8_out0), .out1(decoder_8_out1), .out2(decoder_8_out2), .out3(decoder_8_out3),
    .sel(WriteReg[1:0]), .en(decoder_7_out0));
  Decoder #(.select(2), .disabled(0)) decoder_9 (
    .out0(decoder_9_out0), .out1(decoder_9_out1), .out2(decoder_9_out2), .out3(decoder_9_out3),
    .sel(WriteReg[1:0]), .en(decoder_7_out1));
  Decoder #(.select(2), .disabled(0)) decoder_10 (
    .out0(decoder_10_out0), .out1(decoder_10_out1), .out2(decoder_10_out2), .out3(decoder_10_out3),
    .sel(WriteReg[1:0]), .en(decoder_7_out2));
  Decoder #(.select(2), .disabled(0)) decoder_11 (
    .out0(decoder_11_out0), .out1(decoder_11_out1), .out2(decoder_11_out2), .out3(decoder_11_out3),
    .sel(WriteReg[1:0]), .en(decoder_7_out3));
  Register #(.width(32)) register_16 (.D(WriteData), .en(decoder_8_out0), .Q(register_16_q), .clk(Clk), .clr(Reset));
  Register #(.width(32)) register_17 (.D(WriteData), .en(decoder_8_out1), .Q(register_17_q), .clk(Clk), .clr(Reset));
  Register #(.width(32)) register_18 (.D(WriteData), .en(decoder_8_out2), .Q(register_18_q), .clk(Clk), .clr(Reset));
  Register #(.width(32)) register_19 (.D(WriteData), .en(decoder_8_out3), .Q(register_19_q), .clk(Clk), .clr(Reset));
  Register #(.width(32)) register_20 (.D(WriteData), .en(decoder_9_out0), .Q(register_20_q), .clk(Clk), .clr(Reset));
  Register #(.width(32)) register_21 (.D(WriteData), .en(decoder_9_out1), .Q(register_21_q), .clk(Clk), .clr(Reset));
  Register #(.width(32)) register_22 (.D(WriteData), .en(decoder_9_out2), .Q(register_22_q), .clk(Clk), .clr(Reset));
  Register #(.width(32)) register_23 (.D(WriteData), .en(decoder_9_out3), .Q(register_23_q), .clk(Clk), .clr(Reset));
  Register #(.width(32)) register_24 (.D(WriteData), .en(decoder_10_out0), .Q(register_24_q), .clk(Clk), .clr(Reset));
  Register #(.width(32)) register_25 (.D(WriteData), .en(decoder_10_out1), .Q(register_25_q), .clk(Clk), .clr(Reset));
  Register #(.width(32)) register_26 (.D(WriteData), .en(decoder_10_out2), .Q(register_26_q), .clk(Clk), .clr(Reset));
  Register #(.width(32)) register_27 (.D(WriteData), .en(decoder_10_out3), .Q(register_27_q), .clk(Clk), .clr(Reset));
  Register #(.width(32)) register_28 (.D(WriteData), .en(decoder_11_out0), .Q(register_28_q), .clk(Clk), .clr(Reset));
  Register #(.width(32)) register_29 (.D(WriteData), .en(decoder_11_out1), .Q(register_29_q), .clk(Clk), .clr(Reset));
  Register #(.width(32)) register_30 (.D(WriteData), .en(decoder_11_out2), .Q(register_30_q), .clk(Clk), .clr(Reset));
  Register #(.width(32)) register_31 (.D(WriteData), .en(decoder_11_out3), .Q(register_31_q), .clk(Clk), .clr(Reset));
  // Probe on register_16_q
  // Probe on register_17_q
  // Probe on register_18_q
  // Probe on register_19_q
  // Probe on register_20_q
  // Probe on register_21_q
  // Probe on register_22_q
  // Probe on register_23_q
  // Probe on register_24_q
  // Probe on register_25_q
  // Probe on register_26_q
  // Probe on register_27_q
  // Probe on register_28_q
  // Probe on register_29_q
  // Probe on register_30_q
  // Probe on register_31_q
  Multiplexer #(.width(32), .enable("false")) multiplexer_11 (
    .in0(multiplexer_10_out), .in1(multiplexer_22_out), .out(ReadData1), .sel(ReadReg1[4]));
  Multiplexer #(.width(32), .enable("false")) multiplexer_12 (
    .in0(multiplexer_9_out), .in1(multiplexer_21_out), .out(ReadData2), .sel(ReadReg2[4]));
  Multiplexer #(.select(2), .width(32), .enable("false")) multiplexer_13 (
    .in0(register_16_q), .in1(register_17_q), .in2(register_18_q), .in3(register_19_q),
    .out(multiplexer_13_out), .sel(ReadReg1[1:0]));
  Multiplexer #(.select(2), .width(32), .enable("false")) multiplexer_14 (
    .in0(register_20_q), .in1(register_21_q), .in2(register_22_q), .in3(register_23_q),
    .out(multiplexer_14_out), .sel(ReadReg1[1:0]));
  Multiplexer #(.select(2), .width(32), .enable("false")) multiplexer_15 (
    .in0(register_24_q), .in1(register_25_q), .in2(register_26_q), .in3(register_27_q),
    .out(multiplexer_15_out), .sel(ReadReg1[1:0]));
  Multiplexer #(.select(2), .width(32), .enable("false")) multiplexer_16 (
    .in0(register_28_q), .in1(register_29_q), .in2(register_30_q), .in3(register_31_q),
    .out(multiplexer_16_out), .sel(ReadReg1[1:0]));
  Multiplexer #(.select(2), .width(32), .enable("false")) multiplexer_17 (
    .in0(register_16_q), .in1(register_17_q), .in2(register_18_q), .in3(register_19_q),
    .out(multiplexer_17_out), .sel(ReadReg2[1:0]));
  Multiplexer #(.select(2), .width(32), .enable("false")) multiplexer_18 (
    .in0(register_20_q), .in1(register_21_q), .in2(register_22_q), .in3(register_23_q),
    .out(multiplexer_18_out), .sel(ReadReg2[1:0]));
  Multiplexer #(.select(2), .width(32), .enable("false")) multiplexer_19 (
    .in0(register_24_q), .in1(register_25_q), .in2(register_26_q), .in3(register_27_q),
    .out(multiplexer_19_out), .sel(ReadReg2[1:0]));
  Multiplexer #(.select(2), .width(32), .enable("false")) multiplexer_20 (
    .in0(register_28_q), .in1(register_29_q), .in2(register_30_q), .in3(register_31_q),
    .out(multiplexer_20_out), .sel(ReadReg2[1:0]));
  Multiplexer #(.select(2), .width(32), .enable("false")) multiplexer_21 (
    .in0(multiplexer_17_out), .in1(multiplexer_18_out), .in2(multiplexer_19_out), .in3(multiplexer_20_out),
    .out(multiplexer_21_out), .sel(ReadReg2[3:2]));
  Multiplexer #(.select(2), .width(32), .enable("false")) multiplexer_22 (
    .in0(multiplexer_13_out), .in1(multiplexer_14_out), .in2(multiplexer_15_out), .in3(multiplexer_16_out),
    .out(multiplexer_22_out), .sel(ReadReg1[3:2]));
endmodule

module IMMIDIATE_GENERATION (
  input  [31:0] in_1,
  input  [31:0] in_2,
  output [31:0] out_3,
  output [31:0] out_4,
  output [31:0] out_5
);

  wire [31:0] bit_extender_2_out;

  assign out_3 = {{20{in_1[31]}}, {in_1[31:25], in_1[11:7]}};  // Bit_Extender bit_extender_1
  assign bit_extender_2_out = {{19{in_1[31]}}, {in_1[31], in_1[7], in_1[30:25], in_1[11:8], 1'b0}};  // Bit_Extender bit_extender_2
  assign out_5 = {{20{in_1[31]}}, in_1[31:20]};  // Bit_Extender bit_extender_3
  Adder #(.width(32)) adder_1 (.a(bit_extender_2_out), .b(in_2), .out(out_4));  // open: cin, cout

  // Notes on the sheet:
  //   INSTRUCTION
  //   PC
  //   S-Immediate
  //   SB-Immediate
  //   I-Immediate
endmodule

module ALU_CONTROLLER (
  input  [6:0] OPCODE,
  input  _25th_bit,
  input  branch,
  input  [2:0] ALU_OP,
  input  [31:0] OPERAND_A,
  input  F7,
  input  [31:0] OPERAND_B,
  input  [2:0] F3,
  output out_9,
  output [31:0] \output ,
  output BRANCH_2
);

  wire adder_1_cout, comparator_1_eq, comparator_2_eq, comparator_3_eq, comparator_3_gt, comparator_3_lt,
       comparator_4_eq, comparator_4_gt, comparator_4_lt, comparator_5_eq, comparator_6_eq, not_1_out,
       or_3_out, or_4_out, subtractor_1_bout;
  wire [6:0] multiplexer_1_out, multiplexer_2_out, undriven;
  wire [31:0] adder_1_out, adder_2_out, and_1_out, multiplexer_3_out, multiplexer_4_out, multiplexer_5_out,
       multiplexer_6_out, multiplexer_7_out, multiplexer_8_out, multiplexer_9_out, multiplexer_10_out,
       multiplexer_11_out, multiplexer_12_out, multiplexer_13_out, multiplexer_14_out, multiplexer_15_out,
       multiplexer_16_out, multiplexer_17_out, multiplexer_18_out, multiplexer_20_out, multiplier_1_out,
       or_1_out, shifter_1_out, shifter_2_out, shifter_3_out, subtractor_1_out, xor_1_out;

  Multiplexer #(.select(3), .width(7), .enable("false")) multiplexer_1 (
    .in0(undriven), .in1(undriven), .in2(undriven), .in3(undriven), .in4(7'b0000011), .in5(7'b0100011),
    .in6(undriven), .in7(undriven), .out(multiplexer_1_out), .sel(ALU_OP));
  Multiplexer #(.select(3), .width(7), .enable("false")) multiplexer_2 (
    .in0(7'b0110011), .in1(7'b0010011), .in2(7'b1100011), .in3({7{1'b0}}), .in4({7{1'b0}}), .in5({7{1'b0}}),
    .in6({7{1'b0}}), .in7({7{1'b0}}), .out(multiplexer_2_out), .sel(ALU_OP));
  Comparator #(.width(7)) comparator_1 (.a(OPCODE), .b(multiplexer_1_out), .eq(comparator_1_eq));  // open: gt, lt
  Comparator #(.width(7)) comparator_2 (.a(OPCODE), .b(multiplexer_2_out), .eq(comparator_2_eq));  // open: gt, lt
  Adder #(.width(32)) adder_1 (.a(OPERAND_A), .b(OPERAND_B), .out(adder_1_out), .cout(adder_1_cout));  // open: cin
  Subtractor #(.width(32)) subtractor_1 (
    .a(OPERAND_A), .b(OPERAND_B), .out(subtractor_1_out), .bout(subtractor_1_bout));  // open: bin
  Shifter #(.width(32)) shifter_1 (.in(OPERAND_A), .\dist (OPERAND_B[4:0]), .out(shifter_1_out));
  Comparator #(.width(32)) comparator_3 (
    .a(OPERAND_A), .b(OPERAND_B), .gt(comparator_3_gt), .eq(comparator_3_eq), .lt(comparator_3_lt));
  Comparator #(.width(32), .mode("unsigned")) comparator_4 (
    .a(OPERAND_A), .b(OPERAND_B), .gt(comparator_4_gt), .eq(comparator_4_eq), .lt(comparator_4_lt));
  assign xor_1_out = OPERAND_A ^ OPERAND_B;  // XOR_Gate xor_1, 32 bits wide
  Shifter #(.width(32), .shift("lr")) shifter_2 (.in(OPERAND_A), .\dist (OPERAND_B[4:0]), .out(shifter_2_out));
  Shifter #(.width(32), .shift("ar")) shifter_3 (.in(OPERAND_A), .\dist (OPERAND_B[4:0]), .out(shifter_3_out));
  assign or_1_out = OPERAND_A | OPERAND_B;  // OR_Gate or_1, 32 bits wide
  assign and_1_out = OPERAND_A & OPERAND_B;  // AND_Gate and_1, 32 bits wide
  Adder #(.width(32)) adder_2 (.a(OPERAND_A), .b(OPERAND_B), .out(adder_2_out));  // open: cin, cout
  Multiplexer #(.width(32)) multiplexer_3 (
    .in0(adder_1_out), .in1(subtractor_1_out), .out(multiplexer_3_out), .sel(F7), .en(1'b1));
  Multiplexer #(.width(32), .enable("false")) multiplexer_4 (
    .in0({32{1'b0}}), .in1(32'h1), .out(multiplexer_4_out), .sel(comparator_3_lt));
  Multiplexer #(.width(32), .enable("false")) multiplexer_5 (
    .in0({32{1'b0}}), .in1(32'h1), .out(multiplexer_5_out), .sel(comparator_4_lt));
  Multiplexer #(.width(32)) multiplexer_6 (
    .in0(shifter_2_out), .in1(shifter_3_out), .out(multiplexer_6_out), .sel(F7), .en(1'b1));
  or or_2 (out_9, adder_1_cout, subtractor_1_bout);
  Multiplexer #(.width(32), .enable("false")) multiplexer_7 (
    .in0({32{1'b0}}), .in1(32'h1), .out(multiplexer_7_out), .sel(comparator_3_eq));
  or or_3 (or_3_out, comparator_3_eq, comparator_3_gt);
  Multiplexer #(.width(32), .enable("false")) multiplexer_8 (
    .in0(or_1_out), .in1(multiplexer_5_out), .out(multiplexer_8_out), .sel(branch));
  Multiplexer #(.select(3), .width(32)) multiplexer_9 (
    .in0(adder_2_out), .in1(adder_2_out), .in2(adder_2_out), .in3(adder_2_out), .in4(adder_2_out),
    .in5(adder_2_out), .out(multiplexer_9_out), .sel(F3), .en(comparator_1_eq));  // open: in6, in7
  not not_1 (not_1_out, comparator_3_eq);
  Multiplexer #(.width(32), .enable("false")) multiplexer_10 (
    .in0(xor_1_out), .in1(multiplexer_4_out), .out(multiplexer_10_out), .sel(branch));
  Multiplexer #(.width(32), .enable("false")) multiplexer_11 (
    .in0({32{1'b0}}), .in1(32'h1), .out(multiplexer_11_out), .sel(or_4_out));
  or or_4 (or_4_out, comparator_4_eq, comparator_4_gt);
  Comparator #(.width(7)) comparator_5 (.a(OPCODE), .b(7'b1100011), .eq(comparator_5_eq));  // open: gt, lt
  Comparator #(.width(32)) comparator_6 (.a(\output ), .b(32'h1), .eq(comparator_6_eq));  // open: gt, lt
  Multiplier #(.width(32)) multiplier_1 (.a(OPERAND_A), .b(OPERAND_B), .out(multiplier_1_out));  // open: cin, cout
  Multiplexer #(.width(32), .enable("false")) multiplexer_12 (
    .in0(multiplexer_3_out), .in1(multiplexer_7_out), .out(multiplexer_12_out), .sel(branch));
  Multiplexer #(.width(32), .enable("false")) multiplexer_13 (
    .in0(shifter_1_out), .in1(multiplexer_14_out), .out(multiplexer_13_out), .sel(branch));
  Multiplexer #(.width(32), .enable("false")) multiplexer_14 (
    .in0({32{1'b0}}), .in1(32'h1), .out(multiplexer_14_out), .sel(not_1_out));
  Multiplexer #(.width(32), .enable("false")) multiplexer_15 (
    .in0({32{1'b0}}), .in1(32'h1), .out(multiplexer_15_out), .sel(or_3_out));
  Multiplexer #(.width(32), .enable("false")) multiplexer_16 (
    .in0(multiplexer_11_out), .in1(and_1_out), .out(multiplexer_16_out), .sel(branch));
  and and_2 (BRANCH_2, comparator_5_eq, comparator_6_eq);
  Multiplexer #(.select(3), .width(32)) multiplexer_17 (
    .in0(multiplexer_20_out), .in1(multiplexer_13_out), .in2(multiplexer_4_out), .in3(multiplexer_5_out),
    .in4(multiplexer_10_out), .in5(multiplexer_18_out), .in6(multiplexer_8_out), .in7(multiplexer_16_out),
    .out(multiplexer_17_out), .sel(F3), .en(comparator_2_eq));
  Multiplexer #(.width(32), .enable("false")) multiplexer_18 (
    .in0(multiplexer_6_out), .in1(multiplexer_15_out), .out(multiplexer_18_out), .sel(branch));
  Multiplexer #(.width(32), .enable("false")) multiplexer_19 (
    .in0(multiplexer_9_out), .in1(multiplexer_17_out), .out(\output ), .sel(comparator_2_eq));
  Multiplexer #(.width(32), .enable("false")) multiplexer_20 (
    .in0(multiplexer_12_out), .in1(multiplier_1_out), .out(multiplexer_20_out), .sel(_25th_bit));
  // Probe on \output 

  // Notes on the sheet:
  //                  Operand B
  //                  Operand A
  //   SLT, SLTI , BLT
  //   SLTU, SLTUI, BLTU
  //   ADD, ADDI
  //   SUB
  //   SLL SLLI
  //   XOR,XORI
  //   SRL,SRLI
  //   SRA, SRAI
  //   OR, ORI
  //   AND, ANDI
  //   BEQ
  //   BGE
  //   BGEU
  //   BNE
endmodule

module CONTROL_UNIT (
  input  [6:0] in_1,
  output out_2,
  output out_3,
  output out_4,
  output out_5,
  output out_6,
  output [2:0] out_7,
  output out_8,
  output out_9,
  output out_10
);

  wire type_decode_1_branch, type_decode_1_i_type, type_decode_1_load, type_decode_1_r_type,
       type_decode_1_store;

  TYPE_DECODE type_decode_1 (
    .in_1(in_1), .R_TYPE(type_decode_1_r_type), .LOAD(type_decode_1_load), .STORE(type_decode_1_store),
    .I_TYPE(type_decode_1_i_type), .branch(type_decode_1_branch));
  CONTROL_DECODE control_decode_1 (
    .memwrite(out_2), .memread(out_4), .regwrite(out_5), .memtoreg(out_6), .ALU_OP(out_7),
    .OPERAND_B_SEL(out_8), .EXTEND_SELECT(out_9), .R_type(type_decode_1_r_type), .Load(type_decode_1_load),
    .store(type_decode_1_store), .I_type(type_decode_1_i_type), .branch(type_decode_1_branch),
    .branch_2(out_3), .next_pc_select(out_10));
endmodule
